// Logisim project LC3-2200a.circ as structural Verilog: 6 circuits, main circuit main
module main (
);

  wire ccMatch, clock, DrALU, LdA, LdB, LdCC, LdIR, LdMAR, LdPC;
  wire [1:0] func, writers;
  wire [3:0] regsel;
  wire [4:0] drivers;
  wire [15:0] IR;

  Clock clock_1 (.out(clock));
  MicroController microcontroller_1 (
    .clock(clock), .IR(IR), .ccMatch(ccMatch), .drivers({drivers[4:3], DrALU, drivers[1:0]}),
    .loaders({LdCC, LdB, LdA, LdMAR, LdIR, LdPC}), .writers(writers), .func(func), .regsel(regsel));
  datapath datapath_1 (
    .LdMAR(LdMAR), .LdIR(LdIR), .LdPC(LdPC), .LdA(LdA), .WrREG(writers[0]), .LdB(LdB), .regsel(regsel),
    .func(func), .DrMEM(drivers[1]), .DrALU(DrALU), .DrREG(drivers[0]), .DrOFF(drivers[4]),
    .DrPC(drivers[3]), .LdCC(LdCC), .clock(clock), .WrMEM(writers[1]), .IR(IR), .CCMatch(ccMatch));

  // Other names for the same wires on the sheet: DrREG = drivers[0]; DrMEM = drivers[1]; drivers[2] = DrALU;
  //   DrPC = drivers[3]; DrOFF = drivers[4]; loaders[5:0] = {LdCC, LdB, LdA, LdMAR, LdIR, LdPC}; WrREG = writers[0];
  //   WrMEM = writers[1]

  // Notes on the sheet:
  //   microcontroller
  //   databus
endmodule

module Registers (
  input  [31:0] Din,
  input  WrReg,
  input  clock,
  input  [3:0] regno,
  output [31:0] \output 
);

  wire not_1_out, wr1, wr2, wr3, wr4, wr5, wr6, wr7, wr8, wr9, wr10, wr11, wr12, wr13, wr14, wr15;
  wire [31:0] reg0, reg1, reg2, reg3, reg4, reg5, reg6, reg7, reg8, reg9, reg10, reg11, reg12, reg13, reg14,
       reg15;

  not not_1 (not_1_out, 1'b1);
  Register #(.width(32)) register_1 (.en(not_1_out), .Q(reg0), .clr(1'b1));  // open: D, clk
  Register #(.width(32)) register_2 (.D(Din), .en(wr1), .Q(reg1), .clk(clock));  // open: clr
  Register #(.width(32)) register_3 (.D(Din), .en(wr6), .Q(reg6), .clk(clock));  // open: clr
  Register #(.width(32)) register_4 (.D(Din), .en(wr11), .Q(reg11), .clk(clock));  // open: clr
  Multiplexer #(.select(4), .width(32), .enable("false")) multiplexer_1 (
    .in0(reg0), .in1(reg1), .in2(reg2), .in3(reg3), .in4(reg4), .in5(reg5), .in6(reg6), .in7(reg7),
    .in8(reg8), .in9(reg9), .in10(reg10), .in11(reg11), .in12(reg12), .in13(reg13), .in14(reg15),
    .in15(reg15), .out(\output ), .sel(regno));
  Register #(.width(32)) register_5 (.D(Din), .en(wr2), .Q(reg2), .clk(clock));  // open: clr
  Register #(.width(32)) register_6 (.D(Din), .en(wr7), .Q(reg7), .clk(clock));  // open: clr
  Register #(.width(32)) register_7 (.D(Din), .en(wr12), .Q(reg12), .clk(clock));  // open: clr
  Register #(.width(32)) register_8 (.D(Din), .en(wr3), .Q(reg3), .clk(clock));  // open: clr
  Register #(.width(32)) register_9 (.D(Din), .en(wr8), .Q(reg8), .clk(clock));  // open: clr
  Register #(.width(32)) register_10 (.D(Din), .en(wr13), .Q(reg13), .clk(clock));  // open: clr
  Register #(.width(32)) register_11 (.D(Din), .en(wr4), .Q(reg4), .clk(clock));  // open: clr
  Register #(.width(32)) register_12 (.D(Din), .en(wr9), .Q(reg9), .clk(clock));  // open: clr
  Register #(.width(32)) register_13 (.D(Din), .en(wr14), .Q(reg14), .clk(clock));  // open: clr
  Register #(.width(32)) register_14 (.D(Din), .en(wr10), .Q(reg10), .clk(clock));  // open: clr
  Register #(.width(32)) register_15 (.D(Din), .en(wr15), .Q(reg15), .clk(clock));  // open: clr
  Demultiplexer #(.select(4), .enable("false")) demultiplexer_1 (
    .out1(wr1), .out2(wr2), .out3(wr3), .out4(wr4), .out5(wr5), .out6(wr6), .out7(wr7), .out8(wr8),
    .out9(wr9), .out10(wr10), .out11(wr11), .out12(wr12), .out13(wr13), .out14(wr14), .out15(wr15),
    .in(WrReg), .sel(regno));  // open: out0
  Register #(.width(32)) register_16 (.D(Din), .en(wr5), .Q(reg5), .clk(clock));  // open: clr
endmodule

module ALU (
  input  [31:0] A,
  input  [31:0] B,
  input  [1:0] op,
  output [31:0] \output 
);

  wire [31:0] NAND, shift, shifter_1_out, shifter_2_out, shifter_3_out, tunnel, tunnel_t;

  Shifter #(.width(32), .shift("lr")) shifter_1 (.in(A), .\dist (B[4:0]), .out(shifter_1_out));
  Shifter #(.width(32), .shift("ar")) shifter_2 (.in(A), .\dist (B[4:0]), .out(shifter_2_out));
  Shifter #(.width(32)) shifter_3 (.in(A), .\dist (B[4:0]), .out(shifter_3_out));
  Adder #(.width(32)) adder_1 (.a(A), .b(B), .out(tunnel));  // open: cin, cout
  Adder #(.width(32)) adder_2 (.a(A), .b(32'h1), .out(tunnel_t));  // open: cin, cout
  assign NAND = ~(A & B);  // NAND_Gate nand_1, 32 bits wide
  Multiplexer #(.select(2), .width(32), .enable("false")) multiplexer_1 (
    .in0(shifter_3_out), .in1(shifter_1_out), .in2(shifter_3_out), .in3(shifter_2_out), .out(shift),
    .sel(B[19:18]));
  Multiplexer #(.select(2), .width(32), .enable("false")) multiplexer_2 (
    .in0(tunnel), .in1(NAND), .in2(tunnel_t), .in3(shift), .out(\output ), .sel(op));

  // Other names for the same wires on the sheet: dist5[4:0] = B[4:0]; shiftvecSelect[1:0] = B[19:18]

  // Notes on the sheet:
  //   left shift
  //   logical  right shift
  //   arithmetic right shift
  //   shifting
endmodule

module CheckCC (
  input  [2:0] CurCC,
  input  [2:0] IR,
  output \output 
);

  wire and_1_out, and_2_out, and_3_out;

  and and_1 (and_1_out, CurCC[0], IR[0]);
  and and_2 (and_2_out, CurCC[1], IR[1]);
  and and_3 (and_3_out, CurCC[2], IR[2]);
  or or_1 (\output , and_1_out, and_2_out, and_3_out);
endmodule

module MicroController (
  input  clock,
  input  [15:0] IR,
  input  ccMatch,
  output [4:0] drivers,
  output [5:0] loaders,
  output [1:0] writers,
  output [1:0] func,
  output [3:0] regsel
);

  wire [1:0] REGsel_t, select;
  wire [5:0] checkCC, multiplexer_2_out, next_state, seqROM, State_register_q;

  Multiplexer #(.select(2), .width(4), .enable("false")) multiplexer_1 (
    .in0(IR[11:8]), .in1(IR[7:4]), .in2(IR[3:0]), .out(regsel), .sel(REGsel_t));  // open: in3
  Multiplexer #(.select(2), .width(6)) multiplexer_2 (
    .in0(next_state), .in1(seqROM), .in2(checkCC), .out(multiplexer_2_out), .sel(select));  // open: in3, en
  Register #(.width(6)) State_register (.D(multiplexer_2_out), .Q(State_register_q), .clk(clock));  // open: en, clr
  ROM #(.addrWidth(6), .dataWidth(25)) rom_1 (
    .addr(State_register_q), .data({select, func, REGsel_t, writers, loaders, drivers, next_state}));  // open: sel
  ROM #(.addrWidth(4), .dataWidth(6)) rom_2 (.addr(IR[15:12]), .data(seqROM));  // open: sel
  ROM #(.addrWidth(2), .dataWidth(6)) rom_3 (.addr({1'b0, ccMatch}), .data(checkCC));  // open: sel

  // Other names for the same wires on the sheet: opcode[3:0] = IR[15:12]; RX[3:0] = IR[11:8]; RY[3:0] = IR[7:4];
  //   RZ[3:0] = IR[3:0]

  // Notes on the sheet:
  //   Main Rom
  //   contents of rom_1 (hex, n*v repeats v):
  //   6201 1082 c00900 84044 108045 30100 84047 8408 30100 8404a 10804b 230100 1000000 420e 840f 900 20211
  //   80840 80840 84054 8415 12116 20080 4218 4219 841a 20100 8405c 841d 211e 40040 84060 8421 630100 22
  //   sequencer ROM
  //   contents of rom_2 (hex, n*v repeats v):
  //   3 6 9 c 10 13 18 1b 1f 6*0 22
  //   CheckCC
  //   contents of rom_3 (hex, n*v repeats v):
  //   0 d
endmodule

module datapath (
  input  LdMAR,
  input  LdIR,
  input  LdPC,
  input  LdA,
  input  WrREG,
  input  LdB,
  input  [3:0] regsel,
  input  [1:0] func,
  input  WrMEM,
  input  DrMEM,
  input  DrALU,
  input  DrREG,
  input  DrOFF,
  input  DrPC,
  input  LdCC,
  input  clock,
  output [15:0] IR,
  output CCMatch
);

  wire [2:0] comparator_1_gt, register_1_q;
  wire [19:4] IR_q;
  wire [31:0] A_q, alu_1_output, B_q, bit_extender_1_out, controlled_buffer_1_out, MAR_q, PC_q, ram_1_data,
       registers_1_output;

  Register #(.width(32)) PC (.D(controlled_buffer_1_out), .en(LdPC), .Q(PC_q), .clk(clock));  // open: clr
  assign controlled_buffer_1_out = DrPC ? PC_q : 32'bz;  // Controlled_Buffer controlled_buffer_1
  Comparator #(.width(32)) comparator_1 (
    .a(controlled_buffer_1_out), .b({32{1'b0}}), .gt(comparator_1_gt[0]), .eq(comparator_1_gt[1]),
    .lt(comparator_1_gt[2]));
  Register #(.width(32)) A (.D(controlled_buffer_1_out), .en(LdA), .Q(A_q), .clk(clock));  // open: clr
  ALU alu_1 (.A(A_q), .B(B_q), .op(func), .\output (alu_1_output));
  Register #(.width(3)) register_1 (.D(comparator_1_gt), .en(LdCC), .Q(register_1_q), .clk(clock));  // open: clr
  CheckCC checkcc_1 (.CurCC(register_1_q), .IR(IR[6:4]), .\output (CCMatch));
  Register #(.width(32)) B (.D(controlled_buffer_1_out), .en(LdB), .Q(B_q), .clk(clock));  // open: clr
  assign controlled_buffer_1_out = DrALU ? alu_1_output : 32'bz;  // Controlled_Buffer controlled_buffer_2
  Registers registers_1 (
    .Din(controlled_buffer_1_out), .WrReg(WrREG), .clock(clock), .\output (registers_1_output), .regno(regsel));
  assign controlled_buffer_1_out = DrREG ? registers_1_output : 32'bz;  // Controlled_Buffer controlled_buffer_3
  Register #(.width(32)) MAR (.D(controlled_buffer_1_out), .en(LdMAR), .Q(MAR_q), .clk(clock));  // open: clr
  RAM #(.addrWidth(24), .dataWidth(32), .bus("separate")) ram_1 (
    .addr(MAR_q[23:0]), .din(controlled_buffer_1_out), .data(ram_1_data), .str(WrMEM), .clk(clock));  // open: sel, ld, clr
  assign controlled_buffer_1_out = DrMEM ? ram_1_data : 32'bz;  // Controlled_Buffer controlled_buffer_4
  Register #(.width(32)) u_IR (
    .D(controlled_buffer_1_out), .en(LdIR), .Q({IR[15:4], IR_q, IR[3:0]}), .clk(clock));  // open: clr
  assign bit_extender_1_out = {{12{IR_q[19]}}, {IR_q, IR[3:0]}};  // Bit_Extender bit_extender_1
  assign controlled_buffer_1_out = DrOFF ? bit_extender_1_out : 32'bz;  // Controlled_Buffer controlled_buffer_5

  // Other names for the same wires on the sheet: _0NZP[2:0] = IR[6:4]
endmodule
