// Logisim project lerner_noam.circ as structural Verilog: 12 circuits, main circuit main
module main (
);

  wire BCOND, CLK, comparator_1_eq, comparator_2_eq, comparator_3_eq, Cond, EXSRX, HALT, JCOND, LdMEM,
       or_1_out, stall, WB;
  wire [3:0] DBUF_op, ex_1_op_2, ex_mem_buffer_1_op_2, ex_mem_buffer_1_rx_2, EXrx, IDRA, IDRB, idrr_1_op,
       idrr_1_rx, idrr_ex_buffer_1_rx_2, MEMrx, WBrx;
  wire [31:0] A, B, ex_1_b_2, ex_1_controls_2, ex_1_pc_2, ex_mem_buffer_1_b_2, ex_mem_buffer_1_controls_2,
       ex_mem_buffer_1_pc_2, ex_mem_buffer_1_result_2, EXResult, idrr_1_controls, idrr_1_imm, idrr_1_pc_2,
       idrr_ex_buffer_1_a_2, idrr_ex_buffer_1_b_2, idrr_ex_buffer_1_controls_2, idrr_ex_buffer_1_imm_2,
       idrr_ex_buffer_1_pc_2, if_1_ir, if_1_pc, if_idrr_buffer_1_ir_2, if_idrr_buffer_1_pc_2, mem_1_b_2,
       mem_1_controls_2, mem_1_pc_2, Mem_result, mem_wb_buffer_1_controls_2, trueA, trueB, WBout;

  IF if_1 (
    .clock(CLK), .PC(if_1_pc), .IR(if_1_ir), .BDOND(BCOND), .EXBUF_result(EXResult), .JALRjump(A),
    .JCOND(JCOND), .HALT(HALT), .stall(stall));
  IF_IDRR_Buffer if_idrr_buffer_1 (
    .PC(if_1_pc), .IR(if_1_ir), .JCLR(JCOND), .PC_2(if_idrr_buffer_1_pc_2), .IR_2(if_idrr_buffer_1_ir_2),
    .clock(CLK), .BCLR(BCOND), .stall(stall));
  IDRR idrr_1 (
    .RA(IDRA), .RB(IDRB), .IR(if_idrr_buffer_1_ir_2), .RX(idrr_1_rx), .Imm(idrr_1_imm), .OP(idrr_1_op),
    .controls(idrr_1_controls), .PC(if_idrr_buffer_1_pc_2), .PC_2(idrr_1_pc_2), .JCOND(JCOND), .HALT(HALT));
  ForwardingUnit forwardingunit_1 (
    .RegA(IDRA), .Memout(Mem_result), .Exout(EXResult), .WBout(WBout), .RegB(IDRB), .EXr(EXrx), .MEMr(MEMrx),
    .WBr(WBrx), .B(B), .A(A), .A_2(trueA), .B_2(trueB), .WB(WB), .LdMEM(LdMEM), .EXSRX(EXSRX));
  Dual_Ported_Register_File dual_ported_register_file_1 (
    .CLK(CLK), .WrREGNO(WBrx), .RdREGNO1(IDRA), .RdREGNO2(IDRB), .INPUT(WBout), .OUT1(A), .OUT2(B), .WrEN(WB));
  IDRR_EX_Buffer idrr_ex_buffer_1 (
    .PC(idrr_1_pc_2), .Imm(idrr_1_imm), .OP(idrr_1_op), .RX(idrr_1_rx), .A(trueA), .stall(stall),
    .clock(CLK), .B(trueB), .PC_2(idrr_ex_buffer_1_pc_2), .Imm_2(idrr_ex_buffer_1_imm_2), .OP_2(DBUF_op),
    .RX_2(idrr_ex_buffer_1_rx_2), .A_2(idrr_ex_buffer_1_a_2), .B_2(idrr_ex_buffer_1_b_2),
    .controls(idrr_1_controls), .controls_2(idrr_ex_buffer_1_controls_2));
  Comparator #(.width(4)) comparator_1 (.a(DBUF_op), .b(4'b0101), .eq(comparator_1_eq));  // open: gt, lt
  Comparator #(.width(4)) comparator_2 (.a(EXrx), .b(IDRA), .eq(comparator_2_eq));  // open: gt, lt
  Comparator #(.width(4)) comparator_3 (.a(EXrx), .b(IDRA), .eq(comparator_3_eq));  // open: gt, lt
  or or_1 (or_1_out, comparator_2_eq, comparator_3_eq);
  EX ex_1 (
    .PC(idrr_ex_buffer_1_pc_2), .Imm(idrr_ex_buffer_1_imm_2), .RX(idrr_ex_buffer_1_rx_2), .OP(DBUF_op),
    .A(idrr_ex_buffer_1_a_2), .B(idrr_ex_buffer_1_b_2), .controls(idrr_ex_buffer_1_controls_2), .clock(CLK),
    .RX_2(EXrx), .result(EXResult), .OP_2(ex_1_op_2), .B_2(ex_1_b_2),
    .controls_2({ex_1_controls_2[31:12], Cond, ex_1_controls_2[10:0]}), .PC_2(ex_1_pc_2), .cond(BCOND),
    .EXSRX(EXSRX));
  and and_1 (stall, comparator_1_eq, or_1_out);
  EX_MEM_Buffer ex_mem_buffer_1 (
    .RX(EXrx), .B(ex_1_b_2), .OP(ex_1_op_2), .Result(EXResult), .RX_2(ex_mem_buffer_1_rx_2),
    .B_2(ex_mem_buffer_1_b_2), .OP_2(ex_mem_buffer_1_op_2), .Result_2(ex_mem_buffer_1_result_2),
    .controls({ex_1_controls_2[31:12], Cond, ex_1_controls_2[10:0]}),
    .controls_2(ex_mem_buffer_1_controls_2), .PC(ex_1_pc_2), .PC_2(ex_mem_buffer_1_pc_2), .clock(CLK));
  MEM mem_1 (
    .result(ex_mem_buffer_1_result_2), .B(ex_mem_buffer_1_b_2), .RX(ex_mem_buffer_1_rx_2),
    .OP(ex_mem_buffer_1_op_2), .controls(ex_mem_buffer_1_controls_2), .result_2(Mem_result), .RX_2(MEMrx),
    .controls_2(mem_1_controls_2), .B_2(mem_1_b_2), .PC(ex_mem_buffer_1_pc_2), .PC_2(mem_1_pc_2),
    .clock(CLK), .WrFrMEM(LdMEM));  // open: OP_2
  Clock clock_1 (.out(CLK));
  MEM_WB_Buffer mem_wb_buffer_1 (
    .RX(MEMrx), .Result(Mem_result), .controls(mem_1_controls_2), .RX_2(WBrx), .Result_2(WBout),
    .controls_2({mem_wb_buffer_1_controls_2[31:9], WB, mem_wb_buffer_1_controls_2[7:0]}), .B(mem_1_b_2),
    .PC(mem_1_pc_2), .clock(CLK));  // open: B_2, PC_2
endmodule

module Dual_Ported_Register_File (
  input  CLK,
  input  WrEN,
  input  [3:0] WrREGNO,
  input  [3:0] RdREGNO1,
  input  [3:0] RdREGNO2,
  input  [31:0] INPUT,
  output [31:0] OUT1,
  output [31:0] OUT2
);

  wire En_a0, En_a1, En_a2, En_at, En_fp, En_k0, En_ra, En_s0, En_s1, En_s2, En_sp, En_t0, En_t1, En_t2,
       En_v0;
  wire [31:0] a0, a1, a2, at, fp, k0, ra, s0, s1, s2, sp, t0, t1, t2, v0, zero;

  Decoder #(.select(4), .disabled(0)) decoder_1 (
    .out1(En_at), .out2(En_v0), .out3(En_a0), .out4(En_a1), .out5(En_a2), .out6(En_t0), .out7(En_t1),
    .out8(En_t2), .out9(En_s0), .out10(En_s1), .out11(En_s2), .out12(En_k0), .out13(En_sp), .out14(En_fp),
    .out15(En_ra), .sel(WrREGNO), .en(WrEN));  // open: out0
  Register #(.width(32)) u_zero (.D(INPUT), .en(1'b0), .Q(zero), .clk(CLK));  // open: clr
  Register #(.width(32)) u_at (.D(INPUT), .en(En_at), .Q(at), .clk(CLK));  // open: clr
  Register #(.width(32)) u_v0 (.D(INPUT), .en(En_v0), .Q(v0), .clk(CLK));  // open: clr
  Register #(.width(32)) u_a0 (.D(INPUT), .en(En_a0), .Q(a0), .clk(CLK));  // open: clr
  Register #(.width(32)) u_a1 (.D(INPUT), .en(En_a1), .Q(a1), .clk(CLK));  // open: clr
  Register #(.width(32)) u_a2 (.D(INPUT), .en(En_a2), .Q(a2), .clk(CLK));  // open: clr
  Register #(.width(32)) u_t0 (.D(INPUT), .en(En_t0), .Q(t0), .clk(CLK));  // open: clr
  Register #(.width(32)) u_t1 (.D(INPUT), .en(En_t1), .Q(t1), .clk(CLK));  // open: clr
  Multiplexer #(.select(4), .width(32), .disabled(0), .enable("false")) multiplexer_1 (
    .in0(zero), .in1(at), .in2(v0), .in3(a0), .in4(a1), .in5(a2), .in6(t0), .in7(t1), .in8(t2), .in9(s0),
    .in10(s1), .in11(s2), .in12(k0), .in13(sp), .in14(fp), .in15(ra), .out(OUT2), .sel(RdREGNO2));
  Register #(.width(32)) u_t2 (.D(INPUT), .en(En_t2), .Q(t2), .clk(CLK));  // open: clr
  Register #(.width(32)) u_s0 (.D(INPUT), .en(En_s0), .Q(s0), .clk(CLK));  // open: clr
  Register #(.width(32)) u_s1 (.D(INPUT), .en(En_s1), .Q(s1), .clk(CLK));  // open: clr
  Register #(.width(32)) u_s2 (.D(INPUT), .en(En_s2), .Q(s2), .clk(CLK));  // open: clr
  Register #(.width(32)) u_k0 (.D(INPUT), .en(En_k0), .Q(k0), .clk(CLK));  // open: clr
  Register #(.width(32)) u_sp (.D(INPUT), .en(En_sp), .Q(sp), .clk(CLK));  // open: clr
  Register #(.width(32)) u_fp (.D(INPUT), .en(En_fp), .Q(fp), .clk(CLK));  // open: clr
  Register #(.width(32)) u_ra (.D(INPUT), .en(En_ra), .Q(ra), .clk(CLK));  // open: clr
  Multiplexer #(.select(4), .width(32), .disabled(0), .enable("false")) multiplexer_2 (
    .in0(zero), .in1(at), .in2(v0), .in3(a0), .in4(a1), .in5(a2), .in6(t0), .in7(t1), .in8(t2), .in9(s0),
    .in10(s1), .in11(s2), .in12(k0), .in13(sp), .in14(fp), .in15(ra), .out(OUT1), .sel(RdREGNO1));

  // Notes on the sheet:
  //   MODIFY AT YOUR OWN RISK
endmodule

module IF_IDRR_Buffer (
  input  [31:0] PC,
  input  [31:0] IR,
  input  clock,
  input  JCLR,
  input  BCLR,
  input  stall,
  output [31:0] PC_2,
  output [31:0] IR_2
);

  wire CLEAR_q, CLR, EN;

  not not_1 (EN, stall);
  Register #(.width(32)) u_PC (.D(PC), .en(EN), .Q(PC_2), .clk(clock), .clr(CLR));
  Register #(.width(32)) u_IR (.D(IR), .en(EN), .Q(IR_2), .clk(clock), .clr(CLR));
  Register #(.width(1)) CLEAR (.D(JCLR), .en(EN), .Q(CLEAR_q), .clk(clock), .clr(CLR));
  or or_1 (CLR, CLEAR_q, BCLR);

  // Other names for the same wires on the sheet: CLK = clock
endmodule

module IDRR_EX_Buffer (
  input  [31:0] PC,
  input  [31:0] Imm,
  input  [3:0] OP,
  input  [3:0] RX,
  input  stall,
  input  [31:0] controls,
  input  [31:0] A,
  input  clock,
  input  [31:0] B,
  output [31:0] PC_2,
  output [31:0] Imm_2,
  output [3:0] OP_2,
  output [3:0] RX_2,
  output [31:0] controls_2,
  output [31:0] A_2,
  output [31:0] B_2
);

  wire CLR, undriven;
  wire [3:0] OP_q, RX_q;
  wire [31:0] A_q, B_q, controls_q, Imm_q, PC_q;

  Register #(.width(1)) CLEAR (.D(stall), .en(undriven), .Q(CLR), .clk(clock));  // open: clr
  Controlled_Buffer controlled_buffer_1 ();  // open: in, out, en
  Register #(.width(32)) u_PC (.D(PC), .Q(PC_q), .clk(clock));  // open: en, clr
  Register #(.width(32)) u_Imm (.D(Imm), .Q(Imm_q), .clk(clock));  // open: en, clr
  Register #(.width(4)) u_OP (.D(OP), .Q(OP_q), .clk(clock));  // open: en, clr
  Register #(.width(4)) u_RX (.D(RX), .Q(RX_q), .clk(clock));  // open: en, clr
  Register #(.width(32)) u_A (.D(A), .Q(A_q), .clk(clock));  // open: en, clr
  Register #(.width(32)) u_B (.D(B), .Q(B_q), .clk(clock));  // open: en, clr
  Multiplexer #(.width(32), .enable("false")) multiplexer_1 (.in0(PC_q), .in1({32{1'b0}}), .out(PC_2), .sel(CLR));
  Multiplexer #(.width(32), .enable("false")) multiplexer_2 (.in0(Imm_q), .in1({32{1'b0}}), .out(Imm_2), .sel(CLR));
  Multiplexer #(.width(4), .enable("false")) multiplexer_3 (.in0(OP_q), .in1(4'b0000), .out(OP_2), .sel(CLR));
  Multiplexer #(.width(4), .enable("false")) multiplexer_4 (.in0(RX_q), .in1(4'b0000), .out(RX_2), .sel(CLR));
  Multiplexer #(.width(32), .enable("false")) multiplexer_5 (.in0(A_q), .in1({32{1'b0}}), .out(A_2), .sel(CLR));
  Multiplexer #(.width(32), .enable("false")) multiplexer_6 (.in0(B_q), .in1({32{1'b0}}), .out(B_2), .sel(CLR));
  Register #(.width(32)) u_controls (.D(controls), .Q(controls_q), .clk(clock));  // open: en, clr
  Multiplexer #(.width(32), .enable("false")) multiplexer_7 (
    .in0(controls_q), .in1({32{1'b0}}), .out(controls_2), .sel(CLR));

  // Other names for the same wires on the sheet: CLK = clock
endmodule

module EX_MEM_Buffer (
  input  [3:0] RX,
  input  [31:0] B,
  input  clock,
  input  [3:0] OP,
  input  [31:0] Result,
  input  [31:0] controls,
  input  [31:0] PC,
  output [3:0] RX_2,
  output [31:0] B_2,
  output [3:0] OP_2,
  output [31:0] Result_2,
  output [31:0] controls_2,
  output [31:0] PC_2
);

  wire CLR, EN;

  Register #(.width(4)) u_RX (.D(RX), .en(EN), .Q(RX_2), .clk(clock), .clr(CLR));
  Register #(.width(32)) u_B (.D(B), .en(EN), .Q(B_2), .clk(clock), .clr(CLR));
  Register #(.width(4)) u_OP (.D(OP), .en(EN), .Q(OP_2), .clk(clock), .clr(CLR));
  Register #(.width(32)) u_Result (.D(Result), .en(EN), .Q(Result_2), .clk(clock), .clr(CLR));
  Register #(.width(32)) u_controls (.D(controls), .en(EN), .Q(controls_2), .clk(clock), .clr(CLR));
  Register #(.width(32)) u_PC (.D(PC), .en(EN), .Q(PC_2), .clk(clock), .clr(CLR));

  // Other names for the same wires on the sheet: CLK = clock
endmodule

module MEM_WB_Buffer (
  input  [3:0] RX,
  input  [31:0] Result,
  input  [31:0] controls,
  input  [31:0] B,
  input  clock,
  input  [31:0] PC,
  output [3:0] RX_2,
  output [31:0] Result_2,
  output [31:0] controls_2,
  output [31:0] B_2,
  output [31:0] PC_2
);

  wire B_t, CLR, EN;

  Register #(.width(4)) u_RX (.D(RX), .en(EN), .Q(RX_2), .clk(clock), .clr(CLR));
  Register #(.width(32)) u_Result (.D(Result), .en(EN), .Q(Result_2), .clk(clock), .clr(CLR));
  Register #(.width(32)) u_controls (.D(controls), .en(EN), .Q(controls_2), .clk(clock), .clr(CLR));
  Register #(.width(32)) u_B (.D(B), .en(B_t), .Q(B_2), .clk(B_t), .clr(B_t));
  Register #(.width(32)) u_PC (.D(PC), .en(EN), .Q(PC_2), .clk(clock), .clr(CLR));

  // Other names for the same wires on the sheet: CLK = clock
endmodule

module IDRR (
  input  [31:0] IR,
  input  [31:0] PC,
  output [3:0] RA,
  output [3:0] RB,
  output [3:0] RX,
  output [31:0] Imm,
  output JCOND,
  output [3:0] OP,
  output [31:0] controls,
  output HALT,
  output [31:0] PC_2
);

  assign Imm = {{12{IR[19]}}, IR[19:0]};  // Bit_Extender bit_extender_1
  ROM #(.addrWidth(4), .dataWidth(32)) rom_1 (.addr(IR[31:28]), .data(controls));  // open: sel
  Multiplexer #(.width(4), .enable("false")) multiplexer_1 (
    .in0(IR[3:0]), .in1(IR[27:24]), .out(RB), .sel(controls[0]));
  Comparator #(.width(4)) comparator_1 (.a(IR[31:28]), .b(4'b0100), .eq(JCOND));  // open: gt, lt

  assign HALT = controls[11];
  assign OP = IR[31:28];
  assign PC_2 = PC;
  assign RA = IR[23:20];
  assign RX = IR[27:24];

  // Other names for the same wires on the sheet: SRX = controls[0]

  // Notes on the sheet:
  //   Rz
  //   Ry
  //   contents of rom_1 (hex, n*v repeats v):
  //   100 110 104 33 302 190 510 51 11d 23 6*800
endmodule

module IF (
  input  HALT,
  input  clock,
  input  JCOND,
  input  BDOND,
  input  stall,
  input  [31:0] EXBUF_result,
  input  [31:0] JALRjump,
  output [31:0] PC,
  output [31:0] IR
);

  wire and_1_out, EN, HALT_q, not_1_out, not_3_out;
  wire [23:0] bit_extender_1_out;
  wire [31:0] adder_1_out, PC_q;

  not not_1 (not_1_out, HALT_q);
  not not_2 (EN, stall);
  and and_1 (and_1_out, EN, not_3_out);
  not not_3 (not_3_out, HALT_q);
  Register #(.width(1)) u_HALT (.D(HALT), .en(not_1_out), .Q(HALT_q), .clk(clock));  // open: clr
  Register #(.width(32)) u_PC (.D(PC), .en(and_1_out), .Q(PC_q), .clk(clock));  // open: clr
  Bit_Extender #(.in_width(32), .out_width(24), .\type ("sign")) bit_extender_1 (.in(PC_q), .out(bit_extender_1_out));
  Adder #(.width(32)) adder_1 (.a(PC_q), .b(32'h1), .out(adder_1_out));  // open: cin, cout
  ROM #(.addrWidth(24), .dataWidth(32)) rom_1 (.addr(bit_extender_1_out), .data(IR));  // open: sel
  Multiplexer #(.select(2), .width(32), .enable("false")) multiplexer_1 (
    .in0(adder_1_out), .in1(JALRjump), .in2(EXBUF_result), .out(PC), .sel({BDOND, JCOND}));  // open: in3

  // Other names for the same wires on the sheet: CLK = clock

  // Notes on the sheet:
  //   contents of rom_1 (hex, n*v repeats v):
  //   3000000 1600000a 13300001 936ffffe 0 70000000 54000000 14400001 74000000 946ffffc 0 f0000000
endmodule

module EX (
  input  [31:0] PC,
  input  [31:0] Imm,
  input  [3:0] RX,
  input  [3:0] OP,
  input  [31:0] A,
  input  [31:0] B,
  input  [31:0] controls,
  input  clock,
  output cond,
  output [31:0] result,
  output [3:0] RX_2,
  output [3:0] OP_2,
  output [31:0] PC_2,
  output EXSRX,
  output [31:0] B_2,
  output [31:0] controls_2
);

  wire and_1_out, and_2_out, comparator_1_eq, comparator_2_eq, comparator_3_eq, comparator_4_gt,
       comparator_4_lt, comparator_5_eq, or_1_out;
  wire [31:0] adder_1_out, alu_1_output, multiplexer_1_out, multiplexer_2_out, multiplexer_3_out;

  Comparator #(.width(4)) comparator_1 (.a(OP), .b(4'b0011), .eq(comparator_1_eq));  // open: gt, lt
  Comparator #(.width(32)) comparator_2 (.a(A), .b(B), .eq(comparator_2_eq));  // open: gt, lt
  Comparator #(.width(4)) comparator_3 (.a(OP), .b(4'b1001), .eq(comparator_3_eq));  // open: gt, lt
  Comparator #(.width(32)) comparator_4 (.a(A), .b(B), .gt(comparator_4_gt), .lt(comparator_4_lt));  // open: eq
  and and_1 (and_1_out, comparator_1_eq, comparator_2_eq);
  and and_2 (and_2_out, comparator_3_eq, or_1_out);
  or or_1 (or_1_out, comparator_4_gt, comparator_4_lt);
  or or_2 (cond, and_1_out, and_2_out);
  Multiplexer #(.width(32), .enable("false")) multiplexer_1 (
    .in0(A), .in1(PC), .out(multiplexer_1_out), .sel(controls[10]));
  Multiplexer #(.width(32), .enable("false")) multiplexer_2 (
    .in0(B), .in1(Imm), .out(multiplexer_2_out), .sel(controls[4]));
  Adder #(.width(32)) adder_1 (.a(Imm), .b(PC), .out(adder_1_out));  // open: cin, cout
  Multiplexer #(.width(32), .enable("false")) multiplexer_3 (
    .in0(adder_1_out), .in1(A), .out(multiplexer_3_out), .sel(comparator_5_eq));
  Comparator #(.width(4)) comparator_5 (.a(OP), .b(4'b0100), .eq(comparator_5_eq));  // open: gt, lt
  ALU alu_1 (.A(multiplexer_1_out), .B(multiplexer_2_out), .op(controls[3:2]), .\output (alu_1_output));
  Multiplexer #(.width(32), .enable("false")) multiplexer_4 (
    .in0(alu_1_output), .in1(multiplexer_3_out), .out(result), .sel(controls[1]));

  assign B_2 = B;
  assign controls_2 = controls;
  assign EXSRX = controls[0];
  assign OP_2 = OP;
  assign PC_2 = PC;
  assign RX_2 = RX;

  // Other names for the same wires on the sheet: CLK = clock; JUMP = controls[1]; UseImm = controls[4];
  //   UsePC = controls[10]; func[1:0] = controls[3:2]
endmodule

module ALU (
  input  [31:0] A,
  input  [31:0] B,
  input  [1:0] op,
  output [31:0] \output 
);

  wire [31:0] NAND, shift, shifter_1_out, shifter_2_out, shifter_3_out, tunnel, tunnel_t;

  Shifter #(.width(32), .shift("lr")) shifter_1 (.in(A), .\dist (B[4:0]), .out(shifter_1_out));
  Shifter #(.width(32), .shift("ar")) shifter_2 (.in(A), .\dist (B[4:0]), .out(shifter_2_out));
  Shifter #(.width(32)) shifter_3 (.in(A), .\dist (B[4:0]), .out(shifter_3_out));
  Adder #(.width(32)) adder_1 (.a(A), .b(B), .out(tunnel));  // open: cin, cout
  Adder #(.width(32)) adder_2 (.a(A), .b(32'h1), .out(tunnel_t));  // open: cin, cout
  assign NAND = ~(A & B);  // NAND_Gate nand_1, 32 bits wide
  Multiplexer #(.select(2), .width(32), .enable("false")) multiplexer_1 (
    .in0(shifter_3_out), .in1(shifter_1_out), .in2(shifter_3_out), .in3(shifter_2_out), .out(shift),
    .sel(B[19:18]));
  Multiplexer #(.select(2), .width(32), .enable("false")) multiplexer_2 (
    .in0(tunnel), .in1(NAND), .in2(tunnel_t), .in3(shift), .out(\output ), .sel(op));

  // Other names for the same wires on the sheet: dist5[4:0] = B[4:0]; shiftvecSelect[1:0] = B[19:18]

  // Notes on the sheet:
  //   left shift
  //   logical  right shift
  //   arithmetic right shift
  //   shifting
endmodule

module MEM (
  input  [31:0] result,
  input  [31:0] B,
  input  clock,
  input  [3:0] RX,
  input  [3:0] OP,
  input  [31:0] PC,
  input  [31:0] controls,
  output [31:0] result_2,
  output [3:0] RX_2,
  output [31:0] B_2,
  output [3:0] OP_2,
  output [31:0] PC_2,
  output WrFrMEM,
  output [31:0] controls_2
);

  wire [23:0] bit_extender_1_out;
  wire [31:0] multiplexer_1_out, ram_1_data;

  not not_1 (WrFrMEM, controls[0]);
  Bit_Extender #(.in_width(32), .out_width(24)) bit_extender_1 (.in(result), .out(bit_extender_1_out));
  RAM #(.addrWidth(24), .dataWidth(32), .bus("separate")) ram_1 (
    .addr(bit_extender_1_out), .din(B), .data(ram_1_data), .str(controls[6]), .clk(clock), .ld(controls[7]));  // open: sel, clr
  Multiplexer #(.width(32), .enable("false")) multiplexer_1 (
    .in0(result), .in1(ram_1_data), .out(multiplexer_1_out), .sel(controls[7]));
  Multiplexer #(.width(32), .enable("false")) multiplexer_2 (
    .in0(multiplexer_1_out), .in1(PC), .out(result_2), .sel(controls[9]));

  assign B_2 = B;
  assign controls_2 = controls;
  assign OP_2 = OP;
  assign PC_2 = PC;
  assign RX_2 = RX;

  // Other names for the same wires on the sheet: WtMEM = controls[6]; LdMEM = controls[7]; STRPC = controls[9]
endmodule

module ForwardingUnit (
  input  [3:0] RegA,
  input  [31:0] Memout,
  input  [31:0] Exout,
  input  [31:0] WBout,
  input  [3:0] RegB,
  input  [3:0] EXr,
  input  [3:0] MEMr,
  input  [3:0] WBr,
  input  [31:0] B,
  input  [31:0] A,
  input  WB,
  input  LdMEM,
  input  EXSRX,
  output [31:0] A_2,
  output [31:0] B_2
);

  wire comparator_1_eq, comparator_2_eq, comparator_3_eq, comparator_4_eq, comparator_5_eq, comparator_6_eq,
       comparator_7_eq, comparator_8_eq, not_1_out, not_2_out;
  wire [2:0] and_2_out, and_3_out;
  wire [31:0] multiplexer_1_out, multiplexer_2_out;

  not not_1 (not_1_out, EXSRX);
  Comparator #(.width(4)) comparator_1 (.a(RegB), .b(EXr), .eq(comparator_1_eq));  // open: gt, lt
  not not_2 (not_2_out, EXSRX);
  Comparator #(.width(4)) comparator_2 (.a(RegB), .b(MEMr), .eq(comparator_2_eq));  // open: gt, lt
  and and_1 (and_3_out[1], comparator_2_eq, LdMEM);
  Comparator #(.width(4)) comparator_3 (.a(RegA), .b(EXr), .eq(comparator_3_eq));  // open: gt, lt
  and and_2 (and_2_out[0], comparator_3_eq, not_1_out);
  Comparator #(.width(4)) comparator_4 (.a(RegA), .b(MEMr), .eq(comparator_4_eq));  // open: gt, lt
  Comparator #(.width(4)) comparator_5 (.a(RegA), .b(WBr), .eq(comparator_5_eq));  // open: gt, lt
  and and_3 (and_3_out[0], comparator_1_eq, not_2_out);
  Comparator #(.width(4)) comparator_6 (.a(RegB), .b(WBr), .eq(comparator_6_eq));  // open: gt, lt
  and and_4 (and_2_out[1], comparator_4_eq, LdMEM);
  and and_5 (and_2_out[2], WB, comparator_5_eq);
  and and_6 (and_3_out[2], WB, comparator_6_eq);
  Multiplexer #(.select(3), .width(32), .enable("false")) multiplexer_1 (
    .in0(A), .in1(Exout), .in2(Memout), .in3(Exout), .in4(WBout), .in5(Exout), .in6(Memout), .in7(Exout),
    .out(multiplexer_1_out), .sel(and_2_out));
  Multiplexer #(.select(3), .width(32), .enable("false")) multiplexer_2 (
    .in0(B), .in1(Exout), .in2(Memout), .in3(Exout), .in4(WBout), .in5(Exout), .in6(Memout), .in7(Exout),
    .out(multiplexer_2_out), .sel(and_3_out));
  Comparator #(.width(4)) comparator_7 (.a(RegB), .b(4'b0000), .eq(comparator_7_eq));  // open: gt, lt
  Multiplexer #(.width(32)) multiplexer_3 (
    .in0(multiplexer_1_out), .in1({32{1'b0}}), .out(A_2), .sel(comparator_8_eq));  // open: en
  Comparator #(.width(4)) comparator_8 (.a(RegA), .b(4'b0000), .eq(comparator_8_eq));  // open: gt, lt
  Multiplexer #(.width(32)) multiplexer_4 (
    .in0(multiplexer_2_out), .in1({32{1'b0}}), .out(B_2), .sel(comparator_7_eq));  // open: en
endmodule
